// Logisim project RAM1.circ as structural Verilog: 5 circuits, main circuit main
module main (
);

  D_Flip_Flop d_ff_1 ();  // open: clk, D, Q, Qn, preset, en, reset
  D_Flip_Flop d_ff_2 ();  // open: clk, D, Q, Qn, preset, en, reset
  D_Flip_Flop d_ff_3 ();  // open: clk, D, Q, Qn, preset, en, reset
  D_Flip_Flop d_ff_4 ();  // open: clk, D, Q, Qn, preset, en, reset
  D_Flip_Flop d_ff_5 ();  // open: clk, D, Q, Qn, preset, en, reset
  D_Flip_Flop d_ff_6 ();  // open: clk, D, Q, Qn, preset, en, reset
  Demultiplexer #(.select(4)) demultiplexer_1 ();  // open: out0, out1, out2, out3, out4, out5, out6, out7, out8, out9, out10, out11, out12, out13, out14, out15, in, sel, en
  D_Flip_Flop d_ff_7 ();  // open: clk, D, Q, Qn, preset, en, reset
  Multiplexer #(.select(4)) multiplexer_1 ();  // open: in0, in1, in2, in3, in4, in5, in6, in7, in8, in9, in10, in11, in12, in13, in14, in15, out, sel, en
  D_Flip_Flop d_ff_8 ();  // open: clk, D, Q, Qn, preset, en, reset
  D_Flip_Flop d_ff_9 ();  // open: clk, D, Q, Qn, preset, en, reset
  D_Flip_Flop d_ff_10 ();  // open: clk, D, Q, Qn, preset, en, reset
  D_Flip_Flop d_ff_11 ();  // open: clk, D, Q, Qn, preset, en, reset
  D_Flip_Flop d_ff_12 ();  // open: clk, D, Q, Qn, preset, en, reset
  D_Flip_Flop d_ff_13 ();  // open: clk, D, Q, Qn, preset, en, reset
  D_Flip_Flop d_ff_14 ();  // open: clk, D, Q, Qn, preset, en, reset
  D_Flip_Flop d_ff_15 ();  // open: clk, D, Q, Qn, preset, en, reset
  D_Flip_Flop d_ff_16 ();  // open: clk, D, Q, Qn, preset, en, reset
endmodule

module RAM1 (
  input  [1:0] in_1,
  input  in_2,
  input  in_3,
  input  in_4,
  input  in_5,
  output [15:0] out_6
);

  RAM #(.addrWidth(2), .dataWidth(16)) ram_1 (.addr(in_1), .data(out_6), .sel(in_2), .clk(in_3), .ld(in_4), .clr(in_5));
endmodule

module _1_bits (
  input  A,
  input  B,
  input  Cin,
  output \SỤM ,
  output COUT
);

  wire and_1_out, and_2_out, and_3_out, xor_1_out;

  xor xor_1 (xor_1_out, A, B);
  and and_1 (and_1_out, B, A);
  and and_2 (and_2_out, B, Cin);
  and and_3 (and_3_out, A, Cin);
  or or_1 (COUT, and_1_out, and_2_out, and_3_out);
  xor xor_2 (\SỤM , xor_1_out, Cin);

  // Notes on the sheet:
  //   Mạch cộng 1 bit
endmodule

module Add_Circuit_16_bits (
  input  in_1,
  input  in_2,
  input  in_3,
  input  in_4,
  input  in_5,
  input  in_6,
  input  in_7,
  input  in_8,
  input  in_9,
  input  in_10,
  input  in_11,
  input  in_12,
  input  in_13,
  input  in_14,
  input  in_15,
  input  in_16,
  input  in_17,
  input  in_18,
  input  in_19,
  input  in_20,
  input  in_21,
  input  in_22,
  input  in_23,
  input  in_24,
  input  in_25,
  input  in_26,
  input  in_27,
  input  in_28,
  input  in_29,
  input  in_30,
  input  in_31,
  input  in_32,
  input  in_33,
  output out_34,
  output out_35,
  output out_36,
  output out_37,
  output out_38,
  output out_39,
  output out_40,
  output out_41,
  output out_42,
  output out_43,
  output out_44,
  output out_45,
  output out_46,
  output out_47,
  output out_48,
  output out_49,
  output out_50
);

  wire n1_bits_1_cout, n1_bits_2_cout, n1_bits_3_cout, n1_bits_4_cout, n1_bits_5_cout, n1_bits_6_cout,
       n1_bits_7_cout, n1_bits_8_cout, n1_bits_9_cout, n1_bits_10_cout, n1_bits_11_cout, n1_bits_12_cout,
       n1_bits_13_cout, n1_bits_14_cout, n1_bits_15_cout, xor_1_out, xor_2_out, xor_3_out, xor_4_out,
       xor_5_out, xor_6_out, xor_7_out, xor_8_out, xor_9_out, xor_10_out, xor_11_out, xor_12_out, xor_13_out,
       xor_14_out, xor_15_out, xor_16_out;

  xor xor_1 (xor_1_out, in_9, in_1);
  xor xor_2 (xor_2_out, in_9, in_10);
  xor xor_3 (xor_3_out, in_9, in_18);
  xor xor_4 (xor_4_out, in_9, in_26);
  _1_bits u_1_bits_1 (.A(in_5), .B(xor_1_out), .Cin(in_9), .\SỤM (out_34), .COUT(n1_bits_1_cout));
  _1_bits u_1_bits_2 (.A(in_22), .B(xor_3_out), .Cin(n1_bits_14_cout), .\SỤM (out_42), .COUT(n1_bits_2_cout));
  _1_bits u_1_bits_3 (.A(in_30), .B(xor_4_out), .Cin(n1_bits_15_cout), .\SỤM (out_47), .COUT(n1_bits_3_cout));
  _1_bits u_1_bits_4 (.A(in_14), .B(xor_2_out), .Cin(n1_bits_13_cout), .\SỤM (out_38), .COUT(n1_bits_4_cout));
  xor xor_5 (xor_5_out, in_9, in_19);
  xor xor_6 (xor_6_out, in_9, in_27);
  xor xor_7 (xor_7_out, in_9, in_2);
  xor xor_8 (xor_8_out, in_9, in_11);
  _1_bits u_1_bits_5 (.A(in_31), .B(xor_6_out), .Cin(n1_bits_3_cout), .\SỤM (out_48), .COUT(n1_bits_5_cout));
  _1_bits u_1_bits_6 (.A(in_6), .B(xor_7_out), .Cin(n1_bits_1_cout), .\SỤM (out_35), .COUT(n1_bits_6_cout));
  _1_bits u_1_bits_7 (.A(in_15), .B(xor_8_out), .Cin(n1_bits_4_cout), .\SỤM (out_39), .COUT(n1_bits_7_cout));
  _1_bits u_1_bits_8 (.A(in_23), .B(xor_5_out), .Cin(n1_bits_2_cout), .\SỤM (out_43), .COUT(n1_bits_8_cout));
  xor xor_9 (xor_9_out, in_9, in_20);
  xor xor_10 (xor_10_out, in_9, in_28);
  xor xor_11 (xor_11_out, in_9, in_3);
  xor xor_12 (xor_12_out, in_9, in_12);
  _1_bits u_1_bits_9 (.A(in_24), .B(xor_9_out), .Cin(n1_bits_8_cout), .\SỤM (out_44), .COUT(n1_bits_9_cout));
  _1_bits u_1_bits_10 (.A(in_32), .B(xor_10_out), .Cin(n1_bits_5_cout), .\SỤM (out_49), .COUT(n1_bits_10_cout));
  _1_bits u_1_bits_11 (.A(in_7), .B(xor_11_out), .Cin(n1_bits_6_cout), .\SỤM (out_36), .COUT(n1_bits_11_cout));
  _1_bits u_1_bits_12 (.A(in_16), .B(xor_12_out), .Cin(n1_bits_7_cout), .\SỤM (out_40), .COUT(n1_bits_12_cout));
  xor xor_13 (xor_13_out, in_9, in_4);
  xor xor_14 (xor_14_out, in_9, in_13);
  xor xor_15 (xor_15_out, in_9, in_21);
  xor xor_16 (xor_16_out, in_9, in_29);
  _1_bits u_1_bits_13 (.A(in_8), .B(xor_13_out), .Cin(n1_bits_11_cout), .\SỤM (out_37), .COUT(n1_bits_13_cout));
  _1_bits u_1_bits_14 (.A(in_17), .B(xor_14_out), .Cin(n1_bits_12_cout), .\SỤM (out_41), .COUT(n1_bits_14_cout));
  _1_bits u_1_bits_15 (.A(in_25), .B(xor_15_out), .Cin(n1_bits_9_cout), .\SỤM (out_45), .COUT(n1_bits_15_cout));
  _1_bits u_1_bits_16 (.A(in_33), .B(xor_16_out), .Cin(n1_bits_10_cout), .\SỤM (out_50), .COUT(out_46));
endmodule

module _1_bits_sub (
  input  A,
  input  in_2,
  input  in_3,
  output \SỤM ,
  output COUT
);

  wire and_1_out, and_2_out, and_3_out, not_1_out, xor_1_out;

  not not_1 (not_1_out, in_2);
  xor xor_1 (xor_1_out, A, not_1_out);
  and and_1 (and_1_out, not_1_out, A);
  and and_2 (and_2_out, not_1_out, in_3);
  and and_3 (and_3_out, A, in_3);
  or or_1 (COUT, and_1_out, and_2_out, and_3_out);
  xor xor_2 (\SỤM , xor_1_out, in_3);
endmodule
