// Logisim project btvn.circ as structural Verilog: 1 circuit, main circuit ALU-1bit
module ALU_1bit (
  input  in_1,
  input  in_2,
  input  in_3,
  input  in_4,
  input  in_5,
  output out_6,
  output out_7
);

  wire and_1_out, and_2_out, and_3_out, and_4_out, and_5_out, and_6_out, and_7_out, and_8_out, and_9_out,
       and_10_out, and_11_out, not_1_out, not_2_out, not_3_out, not_4_out, not_5_out, or_1_out, xor_1_out,
       xor_2_out;

  not not_1 (not_1_out, in_2);
  not not_2 (not_2_out, in_4);
  and and_1 (and_1_out, in_1, in_2);
  or or_1 (or_1_out, in_1, in_2);
  not not_3 (not_3_out, in_5);
  not not_4 (not_4_out, in_4);
  not not_5 (not_5_out, in_5);
  and and_2 (and_2_out, not_2_out, not_3_out);
  and and_3 (and_3_out, not_4_out, in_5);
  and and_4 (and_4_out, in_4, not_5_out);
  and and_5 (and_5_out, in_4, in_5);
  and and_6 (and_6_out, and_1_out, and_2_out);
  and and_7 (and_7_out, or_1_out, and_3_out);
  and and_8 (and_8_out, not_1_out, and_4_out);
  and and_9 (and_9_out, and_5_out, in_2, in_1);
  xor xor_1 (xor_1_out, in_1, in_2);
  or or_2 (out_7, and_9_out, and_10_out);
  and and_10 (and_10_out, and_5_out, xor_1_out, in_3);
  buf xor_2 (xor_2_out, xor_1_out);  // XOR_Gate
  and and_11 (and_11_out, xor_2_out, and_5_out);
  or or_3 (out_6, and_6_out, and_7_out, and_11_out, and_8_out);
endmodule
